# Fritzing sketch simulation (saved by Fritzing 0.9.3b)
breadboards: 1

parts:
  Sensor = MAX30102
  PIEZO_(BUZZER) = Piezo Speaker
  Sensor_2 = LM35 Temperature Sensor [package="TO92 [THT]"]
  R1 = Resistor [tolerance=±5% resistance=27k package="0603 [SMD]"]
  NPN = NPN-Transistor [package="SOT-23 [SMD]"]
  Microcontroller = Arduino Uno (Rev3)

nets:
  VIN: Sensor.VIN, PIEZO_(BUZZER).pin2, Sensor_2.+Vs, Microcontroller.5V
  N1: Sensor.SCL, Microcontroller.A5/SCL
  N2: Sensor.SDA, Microcontroller.A4/SDA
  GND: Sensor.GND, Sensor_2.GND, NPN.1, Microcontroller.GND
  N3: PIEZO_(BUZZER).pin1, NPN.2
  N4: Sensor_2.Vout, Microcontroller.A0
  N5: R1.Pin_0, Microcontroller.D3_PWM
  N6: R1.Pin_1, NPN.0

custom parts:
  MAX30102: Oximeter module using the MAX30102 chip. You may wish to read (and check your module) this post on power problems with these modules: https://reedpaper.wordpress.com/2018/08/22/pulse-oximeter-max30100-max30102-how-to-fix-wrong-board/ . As usual, if you want the mounting holes in pcb, you need to drag a hole over the pad in silkscreen to actually drill the hole (by default they are not drilled)
